# Fritzing sketch hackfest2015 (saved by Fritzing 0.9.2b)
perfboards: 12
breadboards: 1

parts:
  rp01 = Raspberry Pi 2
  ar01 = Arduino Mega 2560 (Rev3)
  casino_(lcd01) = 128 x 64 Graphic LCD
  LED2 = smd LED [color="Red (633nm)" package="0805 [SMD]"]
  R2 = Resistor [tolerance=±5% resistance=330 package=THT]
  pipeline_(lcd02) = 128 x 64 Graphic LCD  # not connected
  ar02 = Arduino Uno (Rev3) - ICSP
  solenoid01 = Solenoid  # not connected
  ar03a = Arduino Uno (Rev3) - ICSP
  ar03b = Rotoshield - Motor driver shield for Arduino
  J1 = shrouded pin header, 10 pins [form="♂ (shrouded male)"]  # not connected
  5v = Power plug
  R3 = Photocell (LDR) [package=THT]
  R4 = Resistor [tolerance=±5% resistance=10k package="2512 [SMD]"]
  R1 = Resistor [tolerance=±5% resistance=10k package=THT]
  Q1 = Basic FET N-Channel [package="TO220 [THT]"]  # not connected
  5v1 = Power plug  # not connected
  LED3 = LED - 3mm [color="Red (633nm)" package="3 mm [THT]"]  # not connected
  LED4 = LED - 3mm [color="Red (633nm)" package="3 mm [THT]"]  # not connected
  LED5 = LED - 3mm [color="Red (633nm)" package="3 mm [THT]"]  # not connected
  LED6 = LED - 3mm [color="Red (633nm)" package="3 mm [THT]"]  # not connected
  LED7 = LED - 3mm [color="Red (633nm)" package="3 mm [THT]"]  # not connected
  VALVE1 = Plastic Solenoid Valve  # not connected

nets:
  N1: rp01.GPIO2, ar01.D20/SDA, ar02.A4/SDA
  N2: rp01.GPIO3, ar01.D21/SCL, ar02.A5/SCL
  N3: rp01.GIPO10, ar03a.D11_PWM/MOSI
  N4: rp01.GIPO9, ar03a.D12/MISO
  N5: rp01.GIPO11, ar03a.D13/SCK
  GND: rp01.GND, ar01.GND, casino_(lcd01).1_Vss, casino_(lcd01).15_CS1, casino_(lcd01).20_K(-), ar02.GND, ar03a.GND, ar03b.GND, 5v.GND, R4.Pin_0
  N6: rp01.GIPO8, ar03a.D10_PWM/SS
  N7: ar01.D13_PWM, casino_(lcd01).6_Enable
  N8: ar01.D12_PWM, casino_(lcd01).5_R/W
  N9: ar01.D11_PWM, casino_(lcd01).4_D/I
  N10: ar01.D10_PWM, casino_(lcd01).3_Vo
  N11: ar01.D8_PWM, R2.Pin_1
  VCC: casino_(lcd01).2_Vdd, ar03b.VCC, 5v.VCC, R3.pin_1, R1.Pin_1
  N12: LED2.anode, R2.Pin_0
  N13: ar03a.A0, R3.pin_0, R4.Pin_1
